# Fritzing sketch wiring (saved by Fritzing 0.9.4)
breadboards: 1

parts:
  Part1 = Arduino Uno (Rev3)
  L298N1 = L298N DC motor driver
  Part2 = Thumb Joystick
  Part3 = Thumb Joystick
  U1 = L9110 H-bridge module [part_number="L9110 H-bridge"]  # not connected
  U2 = L9110 H-bridge module [part_number="L9110 H-bridge"]  # not connected
  VCC1 = Battery block 9V

nets:
  N1: Part1.A2, Part3.HORZ
  N2: Part1.A3, Part2.HORZ
  N3: Part1.A4/SDA, Part2.VERT
  N4: Part1.A5/SCL, Part3.VERT
  N5: Part1.D8, Part2.SEL
  GND: Part1.GND, L298N1.GND, Part2.GND, Part3.GND, VCC1.-
  N6: Part1.D2, L298N1.IN1
  N7: Part1.D3_PWM, L298N1.ENA
  N8: Part1.D7, Part3.SEL
  VCC: Part1.5V, Part2.VCC, Part3.VCC
  N9: L298N1.12V, VCC1.+

notes:
  Cables VERT -> VERTICAL
  Cable JAUNE -> HORIZONTAL
  Cable Blanc -> Switch

custom parts:
  L298N DC motor driver: 2x DC motor driver with 78M05 positive voltage regulator (7..35 V) L298N: max 46 V, 2 A Set 5 V Enable jumper to enable 5 V regultor (needed for the L298N) and +5 V output at screw terminal or supply external +5 V at screw terminal Set ENA and/or ENB to +5 V to enable motor permanently or supply ENA and/or ENB with PWM signal IN1 and IN2 set rotation directory for motor A (OUT1/OUT2) IN2 and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
